// Logisim project LFSR.circ as structural Verilog: 1 circuit, main circuit main
module main (
  input  SWITCH1,
  output R11,
  output R12,
  output R13,
  output R14,
  output R15
);

  wire xnor_1_out;

  D_Flip_Flop d_ff_1 (.clk(SWITCH1), .D(xnor_1_out), .Q(R11));  // open: Qn, preset, en, reset
  D_Flip_Flop d_ff_2 (.clk(SWITCH1), .D(R11), .Q(R12));  // open: Qn, preset, en, reset
  D_Flip_Flop d_ff_3 (.clk(SWITCH1), .D(R12), .Q(R13));  // open: Qn, preset, en, reset
  D_Flip_Flop d_ff_4 (.clk(SWITCH1), .D(R13), .Q(R14));  // open: Qn, preset, en, reset
  D_Flip_Flop d_ff_5 (.clk(SWITCH1), .D(R14), .Q(R15));  // open: Qn, preset, en, reset
  xnor xnor_1 (xnor_1_out, R15, R13);
endmodule
