// Logisim project S2-T11.circ as structural Verilog: 1 circuit, main circuit main
module main (
  input  [2:0] LEFT_SHIFT_BY_001
);

  wire and_1_out, and_2_out, and_3_out, and_4_out, and_5_out, and_6_out, and_7_out, and_8_out, and_9_out,
       and_10_out, and_11_out, and_12_out, and_13_out, button_1_out, button_2_out, button_3_out,
       button_4_out, button_5_out, button_6_out, main_1_p2, main_1_p3, main_1_p4, main_1_p5, main_1_p6,
       main_2_p4, main_2_p6, main_2_p8, main_2_p10, main_2_p12, main_3_p2, main_3_p3, main_3_p4, main_3_p5,
       main_3_p6, main_4_o1, main_4_o2, main_4_o3, main_4_o4, main_4_o5, main_5_p2, main_5_p3, main_5_p4,
       main_5_p5, main_5_p6, main_6_o1, main_6_o2, main_6_o3, main_6_o4, main_6_o4_2, not_1_out, not_2_out,
       not_3_out, not_4_out, not_5_out, not_7_out, not_8_out, not_9_out, not_10_out, not_11_out, not_12_out,
       not_13_out, not_14_out, not_15_out, not_16_out, not_17_out;
  wire [0:0] main_2_p15;
  wire [4:0] shifter_1_out, shifter_2_out;

  Button button_1 (.out(button_1_out));
  // LFSR1_main main_1: pin names not known; wires that end beside it: button_1_out, main_1_p2, main_1_p3, main_1_p4, main_1_p5, main_1_p6
  not not_1 (not_1_out, main_2_p10);
  not not_2 (not_2_out, main_2_p6);
  not not_3 (not_3_out, main_2_p4);
  not not_4 (not_4_out, main_2_p8);
  LED O2 (.in(not_2_out));
  LED O3 (.in(not_4_out));
  LED O1 (.in(not_3_out));
  LED O4 (.in(not_1_out));
  // level1copy_main main_2: pin names not known; wires that end beside it: main_1_p2, main_1_p3, main_1_p4, main_2_p4, main_1_p5, main_2_p6, main_1_p6, main_2_p8, 1'b1, main_2_p10, 1'b1, main_2_p12, 1'b1, 1'b1, main_2_p15[0]
  not not_5 (not_5_out, main_2_p12);
  LED O5 (.in(not_5_out));
  and and_1 (and_1_out, main_2_p4, main_2_p6, main_2_p8, main_2_p10);
  and and_2 (and_2_out, and_1_out, main_3_p2);
  and and_3 (and_3_out, and_1_out, main_3_p3);
  Button button_2 (.out(button_2_out));
  not not_6 (main_2_p15[0], 1'b1);
  Button button_3 (.out(button_3_out));
  // LFSR1_main main_3: pin names not known; wires that end beside it: button_3_out, main_3_p2, main_3_p3, main_3_p4, main_3_p5, main_3_p6
  and and_4 (and_4_out, and_1_out, main_3_p4);
  and and_5 (and_5_out, and_1_out, main_3_p5);
  not not_7 (not_7_out, main_4_o3);
  not not_8 (not_8_out, main_4_o2);
  not not_9 (not_9_out, main_4_o1);
  LED O1_2 (.in(not_9_out));
  LED O2_2 (.in(not_8_out));
  LED O3_2 (.in(not_7_out));
  not not_10 (not_10_out, main_4_o5);
  not not_11 (not_11_out, main_4_o4);
  LED O4_2 (.in(not_11_out));
  LED O5_2 (.in(not_10_out));
  Shifter #(.width(5)) shifter_1 (
    .in({4'b1111, main_2_p15[0]}), .\dist (LEFT_SHIFT_BY_001),
    .out({{3{shifter_1_out[4]}}, shifter_1_out[1:0]}));
  and and_6 (and_6_out, and_1_out, main_3_p6);
  level2_main main_4 (
    .R1(and_2_out), .R2(and_3_out), .R3(and_4_out), .R4(and_5_out), .R5(and_6_out), .E1(shifter_1_out[4]),
    .E2(shifter_1_out[4]), .E3(shifter_1_out[4]), .E4(shifter_1_out[1]), .E5(shifter_1_out[0]),
    .O1(main_4_o1), .O2(main_4_o2), .O3(main_4_o3), .SWITCH1(button_2_out), .O4(main_4_o4), .O5(main_4_o5));
  and and_7 (and_7_out, main_4_o1, main_4_o2, main_4_o3);
  and and_8 (and_8_out, and_7_out, main_5_p2);
  Button button_4 (.out(button_4_out));
  Button button_5 (.out(button_5_out));
  not not_12 (not_12_out, main_6_o4);
  not not_13 (not_13_out, main_6_o3);
  not not_14 (not_14_out, main_6_o1);
  not not_15 (not_15_out, main_6_o2);
  LED O2_3 (.in(not_15_out));
  LED O3_3 (.in(not_13_out));
  LED O1_3 (.in(not_14_out));
  LED O4_3 (.in(not_12_out));
  Button button_6 (.out(button_6_out));
  // LFSR1_main main_5: pin names not known; wires that end beside it: button_6_out, main_5_p2, main_5_p3, main_5_p4, main_5_p5, main_5_p6
  and and_9 (and_9_out, and_7_out, main_5_p3);
  not not_16 (not_16_out, main_6_o4_2);
  LED O5_3 (.in(not_16_out));
  Shifter #(.width(5)) shifter_2 (
    .in({{3{shifter_1_out[4]}}, shifter_1_out[1:0]}), .\dist (LEFT_SHIFT_BY_001), .out(shifter_2_out));
  and and_10 (and_10_out, and_7_out, main_5_p4);
  LED led_1 (.in(not_17_out));
  and and_11 (and_11_out, and_7_out, main_5_p5);
  not not_17 (not_17_out, and_13_out);
  level3_main main_6 (
    .R1(and_8_out), .R2(and_9_out), .R3(and_10_out), .R4(and_11_out), .R5(and_12_out), .E1(shifter_2_out[4]),
    .E2(shifter_2_out[3]), .E3(shifter_2_out[2]), .E4(shifter_2_out[1]), .E5(shifter_2_out[0]),
    .O1(main_6_o1), .O2(main_6_o2), .SWITCH2(button_5_out), .O3(main_6_o3), .SWITCH1(button_4_out),
    .O4(main_6_o4), .O4_2(main_6_o4_2));
  and and_12 (and_12_out, and_7_out, main_5_p6);
  and and_13 (and_13_out, main_6_o1, main_6_o2);

  // Notes on the sheet:
  //   SWITCH1
  //   INSTRUCTIONS 
  //   1.Set Subsystem Inputs: 
  //   2.Fault Detection: 
  //   3.Subsystem Recovery:
  //   1: Attempt recovery.
  //   0: Skip recovery.
  //   Recovery Meaning:
  //   4.Monitor Status:
  //   5.Progression:
  //   6.Mission Success:
  //   NOTE:
  //   5-BIT INPUT
  //   FOR LEVEL 1
  //   For Level 1, the expected 5-bit output is constant. 
  //   Crucial: Bit restored to 1 (working state/ON).
  //   Non-crucial: Bit set to 0 (non-working state/OFF).
  //   Dark Green LED: Subsystem working.
  //   Red LED (Light Green Wire): Subsystem not working.
  //   Black LED (Red Wire): The user skipped recovery.
  //   If all levels pass, the Mission Success LED lights up.
  //   on each other whether subsystem is crucial or not
  //   s21
  //   Use switches (Switch1, Switch2, Switch3) to input 5-bit data for each level.
  //   For other levels, the expected output is left-shifted from the previous level. 
  //   A fault is detected if the input doesn't match the expected output. 
  //   Non-crucial Subsystems: Use small switches (s1.x, s2.x, s3.x) to decide:
  //   If any crucial subsystem fails, the mission fails, and the system stops.
  //   The correction within each level  all the 4 subsystems(From LHS) depends
  //   5-BIT EXPECTED OUTPUT
  //   FOR LEVEL  1
  //   Proceeds to the next level if crucial bits are corrected. If not, the mission terminates.
  //   SWITCH2
  //   Crucial Subsystems: Automatically attempts recovery (the first bit is uncorrectable, next three are correctable).
  //   5-BIT INPUT
  //   FOR LEVEL 2
  //   SHIFTER LEFT SHIFTS EXPECTED OUTPUT OF LEVEL 1(11110) BY  1
  //   s31
  //   FOR LEVEL  2
  //   s32
  //   5-BIT EXPECTED OUTPUT
  //   SWITCH3
  //   5-BIT INPUT
  //   FOR LEVEL 3
  //   BLACK WITH GREEN WIRE: 
  //   MISSION SUCCESSFUL
  //   SHIFTER LEFT SHIFTS EXPECTED OUTPUT OF LEVEL 2(11100) BY  1
  //   TEAM DETAILS:
  //   Aalima Khan 231CS201
  //   Bukke Lahari 231CS217
  //   5-BIT EXPECTED OUTPUT
  //   FOR LEVEL 3
  //   Sadipirala Basitha 231CS251
  //   FAULT TOLERANCE IN SPACECRAFTS
endmodule
