// Logisim project level3.circ as structural Verilog: 1 circuit, main circuit main
module main (
  input  R1,
  input  R2,
  input  R3,
  input  R4,
  input  R5,
  input  E1,
  input  E2,
  input  E3,
  input  E4,
  input  E5,
  input  SWITCH2,
  input  SWITCH1,
  output O1,
  output O2,
  output O3,
  output O4,
  output O4_2
);

  wire and_1_out, and_2_out, and_3_out, and_4_out, and_5_out, and_6_out, and_7_out, not_1_out, not_2_out,
       not_3_out, not_4_out, not_5_out, not_6_out, not_7_out, xnor_1_out, xor_1_out, xor_2_out, xor_3_out,
       xor_4_out;

  xor xor_1 (xor_1_out, R1, E1);
  not not_1 (not_1_out, xor_1_out);
  and and_1 (and_1_out, not_1_out, 1'b1);
  not not_2 (not_2_out, and_1_out);
  LED RED_Incorrect_bit_TERMINATE (.in(not_2_out));
  and and_2 (and_2_out, and_1_out, R2);
  xor xor_2 (xor_2_out, and_2_out, E2);
  Multiplexer multiplexer_1 (.in0(and_2_out), .in1(E2), .out(O2), .sel(xor_2_out), .en(and_1_out));
  and and_3 (and_3_out, O2, 1'b1);
  and and_4 (and_4_out, O2, R1);
  and and_5 (and_5_out, and_3_out, R3);
  xor xor_3 (xor_3_out, and_5_out, not_6_out);
  Multiplexer multiplexer_2 (.in0(and_5_out), .in1(not_6_out), .out(O3), .sel(xor_3_out), .en(SWITCH2));
  and and_6 (and_6_out, O3, 1'b1);
  not not_3 (not_3_out, and_4_out);
  and and_7 (and_7_out, and_6_out, R4);
  xor xor_4 (xor_4_out, and_7_out, not_5_out);
  Multiplexer multiplexer_3 (.in0(and_7_out), .in1(not_5_out), .out(O4), .sel(xor_4_out), .en(SWITCH1));
  LED RED_LEVEL3_FAILED_TERMINATE (.in(not_3_out));
  xnor xnor_1 (xnor_1_out, R5, not_7_out);
  not not_4 (not_4_out, xnor_1_out);
  LED RED_NON_ESSENTIAL_SUBSYSTEM_IS_ON (.in(not_4_out));
  not not_5 (not_5_out, E4);
  not not_6 (not_6_out, E3);
  not not_7 (not_7_out, E5);

  assign O1 = R1;
  assign O4_2 = R5;

  // Notes on the sheet:
  //   UNCORRECTABLE
  //   (CRUCIAL
  //   SUBSYSTEM)
  //   CORRECTABLE
  //   (CRUCIAL
  //   SUBSYSTEM)
  //   CORRECTABLE
  //   (NON-CRUCIAL
  //   SUBSYSTEM)
  //   CORRECTABLE
  //   (NON-CRUCIAL
  //   SUBSYSTEM)
  //   NON-ESSENTIAL
  //   SUBSYSTEM
  //   R-RANDOM/INPUT BIT
  //   E-EXPECTED BIT
  //   O-OUTPUT BIT
endmodule
